# Fritzing sketch full_circuit (saved by Fritzing 0.9.3b)
breadboards: 1

parts:
  Part1 = Arduino Uno (Rev3)
  LCD1 = LCD screen
  S1 = Pushbutton [package="[THT]"]
  LED1 = RGB LED (com. cathode, rgb) [package="5 mm [THT]"]
  J1 = Piezo Speaker
  Part2 = Real Time Clock Module - DS1307 RTC Breakout Board
  R1 = Resistor [tolerance=±5% resistance=10k package=THT]
  R2 = Resistor [tolerance=±5% resistance=300 package=THT]
  R3 = Resistor [tolerance=±5% resistance=300 package=THT]
  R4 = Resistor [tolerance=±5% resistance=300 package=THT]
  R5 = Resistor [tolerance=±5% resistance=10k package=THT]  # not connected

nets:
  N1: Part1.A4/SDA, Part2.SDA
  N2: Part1.A5/SCL, Part2.SCL
  N3: Part1.D8, LCD1.DB4
  N4: Part1.D9_PWM, R2.Pin_1
  N5: Part1.D10_PWM/SS, R4.Pin_1
  N6: Part1.D11_PWM/MOSI, LCD1.E
  N7: Part1.D12/MISO, LCD1.RS
  N8: Part1.D2, LCD1.DB7
  N9: Part1.D3_PWM, J1.pin2
  N10: Part1.D4, LCD1.DB6
  N11: Part1.D5_PWM, S1.Pin_1, S1.Pin_2
  N12: Part1.D6_PWM, R3.Pin_1
  N13: Part1.D7, LCD1.DB5
  5V: Part1.5V, LCD1.VDD, LCD1.LED+, S1.Pin_3, S1.Pin_4, Part2.5V, R1.Pin_0
  GND: Part1.GND, LCD1.VSS, LCD1.V0, LCD1.R/W, LCD1.LED-, J1.pin1, Part2.GND, R1.Pin_1
  N14: LED1.red_anode, R4.Pin_0
  N15: LED1.green_anode, R2.Pin_0
  N16: LED1.blue_anode, R3.Pin_0
